# Fritzing sketch Projet_ELEC (saved by Fritzing 0.9.6b)

parts:
  LCD1 = LCD screen
  Mod1 = Raspberry Pi 4B
  Distance_Sensor = HC-SR04 Ultrasonic Distance Sensor
  M2 = DC Motor
  Left_Line_Finder = Grove Light Sensor
  Center_Line_Finder = Grove Light Sensor
  Right_Line_Finder = Grove Light Sensor
  LCM1602_IIC1 = LCM1602 IIC [part_number="LCM1602 IIC" chip_label="LCM1602 IIC" package="DIP (Dual Inline) [THT]"]
  M1 = DC Motor
  Passive_Buzzer = Passive Buzzer
  Motor_Driver = L293D [package=THT]
  part = Battery block 9V

nets:
  VSS: LCD1.VSS, LCM1602_IIC1.VSS
  VDD: LCD1.VDD, LCM1602_IIC1.VDD
  N1: LCD1.V0, LCM1602_IIC1.V0
  N2: LCD1.RS, LCM1602_IIC1.RS
  N3: LCD1.R/W, LCM1602_IIC1.RW
  N4: LCD1.E, LCM1602_IIC1.E
  N5: LCD1.DB0, LCM1602_IIC1.D0
  N6: LCD1.DB1, LCM1602_IIC1.D1
  N7: LCD1.DB2, LCM1602_IIC1.D2
  N8: LCD1.DB3, LCM1602_IIC1.D3
  N9: LCD1.DB4, LCM1602_IIC1.D4
  N10: LCD1.DB5, LCM1602_IIC1.D5
  N11: LCD1.DB6, LCM1602_IIC1.D6
  N12: LCD1.DB7, LCM1602_IIC1.D7
  N13: LCD1.LED+, LCM1602_IIC1.A
  N14: LCD1.LED-, LCM1602_IIC1.K
  VCC: Mod1.3V3, Distance_Sensor.VCC, Left_Line_Finder.VCC, Center_Line_Finder.VCC, Right_Line_Finder.VCC, Passive_Buzzer.NC
  5V: Mod1.5V, LCM1602_IIC1.VCC
  N15: Mod1.GPIO2, LCM1602_IIC1.SDA
  N16: Mod1.GPIO3, LCM1602_IIC1.SCL
  GND: Mod1.GND, Distance_Sensor.GND, Left_Line_Finder.GND, Center_Line_Finder.GND, Right_Line_Finder.GND, LCM1602_IIC1.GND, Passive_Buzzer.-, Motor_Driver.0V, part.-
  N17: Mod1.GPIO14, Passive_Buzzer.S
  N18: Mod1.GPIO17, Right_Line_Finder.SIG
  N19: Mod1.GPIO27, Left_Line_Finder.SIG
  N20: Mod1.GPIO22, Center_Line_Finder.SIG
  N21: Mod1.GPIO25, Distance_Sensor.TRIG
  N22: Mod1.GPIO8, Distance_Sensor.ECHO
  N23: Mod1.GPIO5, Motor_Driver.In_1
  N24: Mod1.GPIO6, Motor_Driver.In_2
  N25: Mod1.GPIO12, Motor_Driver.Enable_2
  N26: Mod1.GPIO13, Motor_Driver.Enable_1
  N27: Mod1.GPIO26, Motor_Driver.In_3
  N28: Mod1.GPIO21, Motor_Driver.In_4
  N29: M2.pin_1, Motor_Driver.Out_4_(_Controlled_by_Enable_2_)
  N30: M2.pin_2, Motor_Driver.Out_3_(_Controlled_by_Enable_2_)
  N31: M1.pin_1, Motor_Driver.Out_2_(_Controlled_by_Enable_1_)
  N32: M1.pin_2, Motor_Driver.Out_1_(_Controlled_by_Enable_1_)
  N33: Motor_Driver.+Vmotor, part.+

custom parts:
  LCM1602 IIC: I2C-Module to use a 1602 or 2004 LCD on with the wire.h libory Serial LCD Modul
